// Logisim project N2T.circ as structural Verilog: 14 circuits, main circuit PC
module computer (
  input  reset,
  output [15:0] out_2,
  output [15:0] out_3
);

  wire clk, cpu_1_writem;
  wire [14:0] cpu_1_addressm, cpu_1_pc_out;
  wire [15:0] cpu_1_outm, rom_1_data;

  ROM #(.addrWidth(15), .dataWidth(16)) rom_1 (.addr(cpu_1_pc_out), .data(rom_1_data));
  Clock clock_1 (.out(clk));
  cpu cpu_1 (
    .inM(out_3), .instruction(rom_1_data), .clk(clk), .rst(reset), .dout(out_2), .PC_out(cpu_1_pc_out),
    .outM(cpu_1_outm), .writeM(cpu_1_writem), .addressM(cpu_1_addressm));
  RAM #(.addrWidth(15), .dataWidth(16), .enables("line"), .\type ("nonvolatile")) ram_1 (
    .addr(cpu_1_addressm), .we(cpu_1_writem), .clk(clk), .din(cpu_1_outm), .dout(out_3));

  // Notes on the sheet:
  //   contents of rom_1 (hex, n*v repeats v):
  //   0 fc10 10 e308 11 efc8 2 ea88 11 fc10 10 f4d0 16 e301 1 fc10 2 f088 11 fdc8 8 ea86 16 ea87
endmodule

module cpu (
  input  [15:0] inM,
  input  [15:0] instruction,
  input  rst,
  input  clk,
  output [15:0] dout,
  output [15:0] outM,
  output writeM,
  output [14:0] addressM,
  output [14:0] PC_out
);

  wire and_3_out, and_4_out, and_5_out, equal, greater, j1, j2, j3, ld, less, ng, not_1_out, not_2_out,
       not_3_out, not_4_out, or_1_out, or_2_out, or_3_out;
  wire [14:4] multiplexer_1_out;
  wire [15:0] multiplexer_2_out, multiplexer_3_out, multiplexer_4_out;
  wire [15:15] aout, pc_1_out_6;

  Multiplexer #(.width(16)) multiplexer_1 (
    .in0({16{1'b0}}), .in1(instruction), .out({ld, multiplexer_1_out, writeM, j3, j2, j1}),
    .sel(instruction[15]));
  Multiplexer #(.width(16)) multiplexer_2 (.in0(instruction), .in1(outM), .out(multiplexer_2_out), .sel(ld));
  regist regist_1 (.inp(multiplexer_2_out), .load(or_1_out), .clk(clk), .out_4({aout[15], addressM}));
  or or_1 (or_1_out, multiplexer_1_out[5], not_1_out);
  not not_1 (not_1_out, ld);
  Multiplexer #(.width(16)) multiplexer_3 (
    .in0({16{1'b0}}), .in1(outM), .out(multiplexer_3_out), .sel(multiplexer_1_out[4]));
  regist regist_2 (.inp(multiplexer_3_out), .load(multiplexer_1_out[4]), .clk(clk), .out_4(dout));
  not not_2 (not_2_out, ng);
  and and_1 (greater, not_2_out, not_3_out);
  not not_3 (not_3_out, equal);
  and and_2 (less, ng, not_4_out);
  not not_4 (not_4_out, equal);
  Multiplexer #(.width(16)) multiplexer_4 (
    .in0({aout[15], addressM}), .in1(inM), .out(multiplexer_4_out), .sel(multiplexer_1_out[12]));
  alu alu_1 (
    .in_3(multiplexer_1_out[11]), .in_4(multiplexer_1_out[10]), .in_5(multiplexer_1_out[9]), .x(dout),
    .y(multiplexer_4_out), .in_6(multiplexer_1_out[8]), .in_7(multiplexer_1_out[7]),
    .in_8(multiplexer_1_out[6]), .ng(ng), .o(outM), .zr(equal));
  and and_3 (and_3_out, j1, greater);
  and and_4 (and_4_out, j2, equal);
  and and_5 (and_5_out, j3, less);
  PC pc_1 (
    .in_1(1'b1), .in_2(or_3_out), .in_3(rst), .in_5({aout[15], addressM}), .clk(clk),
    .out_6({pc_1_out_6[15], PC_out}));
  or or_2 (or_2_out, and_3_out, and_4_out);
  or or_3 (or_3_out, or_2_out, and_5_out);

  // Other names for the same wires on the sheet: d1 = writeM; aout[14:0] = addressM; zr = equal

  // Notes on the sheet:
  //   A register
  //   D register
endmodule

module ram16k (
  input  [13:0] addr,
  input  load,
  input  clk,
  input  [15:0] inp,
  output [15:0] outp
);

  RAM #(.addrWidth(14), .dataWidth(16), .trigger("falling")) ram_1 (
    .addr(addr), .we(load), .oe(1'b1), .clk(clk), .din(inp), .dout(outp));
endmodule

module ram64 (
  input  [15:0] in_1,
  input  load,
  input  [5:0] address,
  input  clk,
  output [15:0] out_5
);

  wire demultiplexer_1_out0, demultiplexer_1_out1, demultiplexer_1_out2, demultiplexer_1_out3,
       demultiplexer_1_out4, demultiplexer_1_out5, demultiplexer_1_out6, demultiplexer_1_out7;
  wire [15:0] ram8_1_out_5, ram8_2_out_5, ram8_3_out_5, ram8_4_out_5, ram8_5_out_5, ram8_6_out_5,
       ram8_7_out_5, ram8_8_out_5;

  Demultiplexer #(.select(3)) demultiplexer_1 (
    .out0(demultiplexer_1_out0), .out1(demultiplexer_1_out1), .out2(demultiplexer_1_out2),
    .out3(demultiplexer_1_out3), .out4(demultiplexer_1_out4), .out5(demultiplexer_1_out5),
    .out6(demultiplexer_1_out6), .out7(demultiplexer_1_out7), .in(load), .sel(address[5:3]));
  ram8 ram8_1 (.inp(in_1), .address(address[2:0]), .load(demultiplexer_1_out0), .clk(clk), .out_5(ram8_1_out_5));
  ram8 ram8_2 (.inp(in_1), .address(address[2:0]), .load(demultiplexer_1_out1), .clk(clk), .out_5(ram8_2_out_5));
  ram8 ram8_3 (.inp(in_1), .address(address[2:0]), .load(demultiplexer_1_out2), .clk(clk), .out_5(ram8_3_out_5));
  ram8 ram8_4 (.inp(in_1), .address(address[2:0]), .load(demultiplexer_1_out3), .clk(clk), .out_5(ram8_4_out_5));
  ram8 ram8_5 (.inp(in_1), .address(address[2:0]), .load(demultiplexer_1_out4), .clk(clk), .out_5(ram8_5_out_5));
  ram8 ram8_6 (.inp(in_1), .address(address[2:0]), .load(demultiplexer_1_out5), .clk(clk), .out_5(ram8_6_out_5));
  ram8 ram8_7 (.inp(in_1), .address(address[2:0]), .load(demultiplexer_1_out6), .clk(clk), .out_5(ram8_7_out_5));
  ram8 ram8_8 (.inp(in_1), .address(address[2:0]), .load(demultiplexer_1_out7), .clk(clk), .out_5(ram8_8_out_5));
  Multiplexer #(.select(3), .width(16)) multiplexer_1 (
    .in0(ram8_1_out_5), .in1(ram8_2_out_5), .in2(ram8_3_out_5), .in3(ram8_4_out_5), .in4(ram8_5_out_5),
    .in5(ram8_6_out_5), .in6(ram8_7_out_5), .in7(ram8_8_out_5), .out(out_5), .sel(address[5:3]));

  // Other names for the same wires on the sheet: lowadd[2:0] = address[2:0]; inp[15:0] = in_1
endmodule

module ram8 (
  input  [15:0] inp,
  input  load,
  input  [2:0] address,
  input  clk,
  output [15:0] out_5
);

  wire demultiplexer_1_out0, demultiplexer_1_out1, demultiplexer_1_out2, demultiplexer_1_out3,
       demultiplexer_1_out4, demultiplexer_1_out5, demultiplexer_1_out6, demultiplexer_1_out7;
  wire [15:0] regist_1_out_4, regist_2_out_4, regist_3_out_4, regist_4_out_4, regist_5_out_4, regist_6_out_4,
       regist_7_out_4, regist_8_out_4;

  Demultiplexer #(.select(3)) demultiplexer_1 (
    .out0(demultiplexer_1_out0), .out1(demultiplexer_1_out1), .out2(demultiplexer_1_out2),
    .out3(demultiplexer_1_out3), .out4(demultiplexer_1_out4), .out5(demultiplexer_1_out5),
    .out6(demultiplexer_1_out6), .out7(demultiplexer_1_out7), .in(load), .sel(address));
  regist regist_1 (.inp(inp), .load(demultiplexer_1_out0), .clk(clk), .out_4(regist_1_out_4));
  regist regist_2 (.inp(inp), .load(demultiplexer_1_out1), .clk(clk), .out_4(regist_2_out_4));
  regist regist_3 (.inp(inp), .load(demultiplexer_1_out2), .clk(clk), .out_4(regist_3_out_4));
  regist regist_4 (.inp(inp), .load(demultiplexer_1_out3), .clk(clk), .out_4(regist_4_out_4));
  regist regist_5 (.inp(inp), .load(demultiplexer_1_out4), .clk(clk), .out_4(regist_5_out_4));
  regist regist_6 (.inp(inp), .load(demultiplexer_1_out5), .clk(clk), .out_4(regist_6_out_4));
  regist regist_7 (.inp(inp), .load(demultiplexer_1_out6), .clk(clk), .out_4(regist_7_out_4));
  regist regist_8 (.inp(inp), .load(demultiplexer_1_out7), .clk(clk), .out_4(regist_8_out_4));
  Multiplexer #(.select(3), .width(16)) multiplexer_1 (
    .in0(regist_1_out_4), .in1(regist_2_out_4), .in2(regist_3_out_4), .in3(regist_4_out_4),
    .in4(regist_5_out_4), .in5(regist_6_out_4), .in6(regist_7_out_4), .in7(regist_8_out_4), .out(out_5),
    .sel(address));
endmodule

module PC (
  input  in_1,
  input  in_2,
  input  in_3,
  input  clk,
  input  [15:0] in_5,
  output [15:0] out_6
);

  wire [15:0] inc16_1_out_2, multiplexer_1_out, multiplexer_2_out, multiplexer_3_out;

  inc16 inc16_1 (.in_1(out_6), .out_2(inc16_1_out_2));
  Multiplexer #(.width(16)) multiplexer_1 (.in0(out_6), .in1(inc16_1_out_2), .out(multiplexer_1_out), .sel(in_1));
  Multiplexer #(.width(16)) multiplexer_2 (.in0(multiplexer_1_out), .in1(in_5), .out(multiplexer_2_out), .sel(in_2));
  Multiplexer #(.width(16)) multiplexer_3 (
    .in0(multiplexer_2_out), .in1({16{1'b0}}), .out(multiplexer_3_out), .sel(in_3));
  regist regist_1 (.inp(multiplexer_3_out), .load(1'b1), .clk(clk), .out_4(out_6));

  // Other names for the same wires on the sheet: inc = in_1; INP[15:0] = in_5; load = in_2; rst = in_3
endmodule

module regist (
  input  [15:0] inp,
  input  clk,
  input  load,
  output [15:0] out_4
);

  \bit  bit_1 (.Inp(inp[0]), .load(load), .clk(clk), .OUTP(out_4[0]));
  \bit  bit_2 (.Inp(inp[1]), .load(load), .clk(clk), .OUTP(out_4[1]));
  \bit  bit_3 (.Inp(inp[2]), .load(load), .clk(clk), .OUTP(out_4[2]));
  \bit  bit_4 (.Inp(inp[3]), .load(load), .clk(clk), .OUTP(out_4[3]));
  \bit  bit_5 (.Inp(inp[4]), .load(load), .clk(clk), .OUTP(out_4[4]));
  \bit  bit_6 (.Inp(inp[5]), .load(load), .clk(clk), .OUTP(out_4[5]));
  \bit  bit_7 (.Inp(inp[6]), .load(load), .clk(clk), .OUTP(out_4[6]));
  \bit  bit_8 (.Inp(inp[7]), .load(load), .clk(clk), .OUTP(out_4[7]));
  \bit  bit_9 (.Inp(inp[8]), .load(load), .clk(clk), .OUTP(out_4[8]));
  \bit  bit_10 (.Inp(inp[9]), .load(load), .clk(clk), .OUTP(out_4[9]));
  \bit  bit_11 (.Inp(inp[10]), .load(load), .clk(clk), .OUTP(out_4[10]));
  \bit  bit_12 (.Inp(inp[11]), .load(load), .clk(clk), .OUTP(out_4[11]));
  \bit  bit_13 (.Inp(inp[12]), .load(load), .clk(clk), .OUTP(out_4[12]));
  \bit  bit_14 (.Inp(inp[13]), .load(load), .clk(clk), .OUTP(out_4[13]));
  \bit  bit_15 (.Inp(inp[14]), .load(load), .clk(clk), .OUTP(out_4[14]));
  \bit  bit_16 (.Inp(inp[15]), .load(load), .clk(clk), .OUTP(out_4[15]));
endmodule

module \bit  (
  input  Inp,
  input  load,
  input  clk,
  output OUTP
);

  wire multiplexer_1_out;

  Multiplexer multiplexer_1 (.in0(OUTP), .in1(Inp), .out(multiplexer_1_out), .sel(load));
  d_ff d_ff_1 (.clk(clk), .s(multiplexer_1_out), .Q(OUTP));  // open: Qb
endmodule

module d_ff (
  input  s,
  input  clk,
  output Q,
  output Qb
);

  wire nand_1_out, nand_2_out, nand_3_out, nand_4_out, nand_5_out, nand_6_out, not_1_out, not_2_out,
       not_3_out;

  not not_1 (not_1_out, s);
  nand nand_1 (nand_1_out, s, clk);
  nand nand_2 (nand_2_out, clk, not_1_out);
  not not_2 (not_2_out, clk);
  nand nand_3 (nand_3_out, nand_1_out, nand_4_out);
  nand nand_4 (nand_4_out, nand_3_out, nand_2_out);
  not not_3 (not_3_out, nand_3_out);
  nand nand_5 (nand_5_out, nand_3_out, not_2_out);
  nand nand_6 (nand_6_out, not_2_out, not_3_out);
  nand nand_7 (Q, nand_5_out, Qb);
  nand nand_8 (Qb, Q, nand_6_out);
endmodule

module alu (
  input  [15:0] x,
  input  [15:0] y,
  input  in_3,
  input  in_4,
  input  in_5,
  input  in_6,
  input  in_7,
  input  in_8,
  output [15:0] o,
  output zr,
  output ng
);

  wire or_1_out, or_2_out, or_3_out;
  wire [15:0] add16_1_out_3, and_1_out, multiplexer_1_out, multiplexer_2_out, multiplexer_5_out, not_1_out,
       not_2_out, not_3_out, readyx, readyy;

  Multiplexer #(.width(16)) multiplexer_1 (.in0(x), .in1({16{1'b0}}), .out(multiplexer_1_out), .sel(in_3));
  Multiplexer #(.width(16)) multiplexer_2 (.in0(y), .in1({16{1'b0}}), .out(multiplexer_2_out), .sel(in_5));
  assign not_1_out = ~multiplexer_1_out;  // NOT_Gate not_1, 16 bits wide
  assign not_2_out = ~multiplexer_2_out;  // NOT_Gate not_2, 16 bits wide
  Multiplexer #(.width(16)) multiplexer_3 (.in0(multiplexer_2_out), .in1(not_2_out), .out(readyy), .sel(in_6));
  Multiplexer #(.width(16)) multiplexer_4 (.in0(multiplexer_1_out), .in1(not_1_out), .out(readyx), .sel(in_4));
  assign and_1_out = readyx & readyy;  // AND_Gate and_1, 16 bits wide
  add16 add16_1 (.in_1(readyx), .in_2(readyy), .out_3(add16_1_out_3));
  Multiplexer #(.width(16)) multiplexer_5 (.in0(and_1_out), .in1(add16_1_out_3), .out(multiplexer_5_out), .sel(in_7));
  assign not_3_out = ~multiplexer_5_out;  // NOT_Gate not_3, 16 bits wide
  or or_1 (or_1_out, o[0], o[1], o[2], o[3], o[4], o[5], o[6], o[7]);
  or or_2 (or_2_out, o[8], o[9], o[10], o[11], o[12], o[13], o[14], ng);
  Multiplexer #(.width(16)) multiplexer_6 (.in0(multiplexer_5_out), .in1(not_3_out), .out({ng, o[14:0]}), .sel(in_8));
  or or_3 (or_3_out, or_1_out, or_2_out);
  not not_4 (zr, or_3_out);

  assign o[15] = ng;

  // Other names for the same wires on the sheet: f = in_7; no = in_8; nx = in_4; ny = in_6;
  //   readyout[15:0] = {ng, o[14:0]}; zx = in_3; zy = in_5
endmodule

module inc16 (
  input  [15:0] in_1,
  output [15:0] out_2
);

  add16 add16_1 (.in_1(in_1), .in_2(16'h1), .out_3(out_2));
endmodule

module add16 (
  input  [15:0] in_1,
  input  [15:0] in_2,
  output [15:0] out_3
);

  wire full_addr_1_carry, full_addr_2_carry, full_addr_3_carry, full_addr_4_carry, full_addr_5_carry,
       full_addr_6_carry, full_addr_7_carry, full_addr_8_carry, full_addr_9_carry, full_addr_10_carry,
       full_addr_11_carry, full_addr_12_carry, full_addr_13_carry, full_addr_14_carry, full_addr_15_carry;

  full_addr full_addr_1 (.a(in_1[0]), .b(in_2[0]), .c(1'b0), .sum(out_3[0]), .carry(full_addr_1_carry));
  full_addr full_addr_2 (.a(in_1[1]), .b(in_2[1]), .c(full_addr_1_carry), .sum(out_3[1]), .carry(full_addr_2_carry));
  full_addr full_addr_3 (.a(in_1[2]), .b(in_2[2]), .c(full_addr_2_carry), .sum(out_3[2]), .carry(full_addr_3_carry));
  full_addr full_addr_4 (.a(in_1[3]), .b(in_2[3]), .c(full_addr_3_carry), .sum(out_3[3]), .carry(full_addr_4_carry));
  full_addr full_addr_5 (.a(in_1[4]), .b(in_2[4]), .c(full_addr_4_carry), .sum(out_3[4]), .carry(full_addr_5_carry));
  full_addr full_addr_6 (.a(in_1[5]), .b(in_2[5]), .c(full_addr_5_carry), .sum(out_3[5]), .carry(full_addr_6_carry));
  full_addr full_addr_7 (.a(in_1[6]), .b(in_2[6]), .c(full_addr_6_carry), .sum(out_3[6]), .carry(full_addr_7_carry));
  full_addr full_addr_8 (.a(in_1[7]), .b(in_2[7]), .c(full_addr_7_carry), .sum(out_3[7]), .carry(full_addr_8_carry));
  full_addr full_addr_9 (.a(in_1[8]), .b(in_2[8]), .c(full_addr_8_carry), .sum(out_3[8]), .carry(full_addr_9_carry));
  full_addr full_addr_10 (.a(in_1[9]), .b(in_2[9]), .c(full_addr_9_carry), .sum(out_3[9]), .carry(full_addr_10_carry));
  full_addr full_addr_11 (
    .a(in_1[10]), .b(in_2[10]), .c(full_addr_10_carry), .sum(out_3[10]), .carry(full_addr_11_carry));
  full_addr full_addr_12 (
    .a(in_1[11]), .b(in_2[11]), .c(full_addr_11_carry), .sum(out_3[11]), .carry(full_addr_12_carry));
  full_addr full_addr_13 (
    .a(in_1[12]), .b(in_2[12]), .c(full_addr_12_carry), .sum(out_3[12]), .carry(full_addr_13_carry));
  full_addr full_addr_14 (
    .a(in_1[13]), .b(in_2[13]), .c(full_addr_13_carry), .sum(out_3[13]), .carry(full_addr_14_carry));
  full_addr full_addr_15 (
    .a(in_1[14]), .b(in_2[14]), .c(full_addr_14_carry), .sum(out_3[14]), .carry(full_addr_15_carry));
  full_addr full_addr_16 (.a(in_1[15]), .b(in_2[15]), .c(full_addr_15_carry), .sum(out_3[15]));  // open: carry
endmodule

module full_addr (
  input  a,
  input  b,
  input  c,
  output sum,
  output carry
);

  wire half_addr_1_carry, half_addr_1_sum, half_addr_2_carry;

  half_addr half_addr_1 (.a(a), .b(b), .sum(half_addr_1_sum), .carry(half_addr_1_carry));
  half_addr half_addr_2 (.a(half_addr_1_sum), .b(c), .sum(sum), .carry(half_addr_2_carry));
  or or_1 (carry, half_addr_2_carry, half_addr_1_carry);
endmodule

module half_addr (
  input  a,
  input  b,
  output sum,
  output carry
);

  xor xor_1 (sum, a, b);
  and and_1 (carry, a, b);
endmodule
